// Logisim project Microprocessor356.circ as structural Verilog: 29 circuits, main circuit Microprocessor
module Next_Line_Counter (
  input  [15:0] Last_Line,
  input  [15:0] Machine_Code,
  input  [15:0] Read_2,
  input  [4:0] Flags_In,
  output [15:0] PC_1,
  output [15:0] Next_Line,
  output [15:0] PCforContext
);

  wire bitselector_2_out, comparator_2_eq, comparator_3_eq, comparator_5_eq, comparator_6_eq, Doing_C_R,
       Halt, multiplexer_2_out, not_1_out, not_2_out, not_3_out, not_4_out, not_5_out, not_6_out, not_7_out,
       not_8_out, not_9_out, or_1_out, or_2_out, or_3_out, or_4_out, xor_1_out;
  wire [3:0] bitselector_3_out;
  wire [7:0] bitselector_1_out;
  wire [15:0] adder_2_out, bit_extender_1_out, Branch_line, multiplexer_1_out, multiplexer_4_out,
       register_2_q;

  xor xor_1 (xor_1_out, Flags_In[0], Flags_In[2]);
  Comparator #(.width(16)) comparator_1 (.a(Machine_Code), .b({16{1'b0}}), .eq(Halt));  // open: gt, lt
  or or_1 (or_1_out, xor_1_out, Flags_In[1]);
  BitSelector #(.width(16), .group(8)) bitselector_1 (.in(Machine_Code), .out(bitselector_1_out), .sel(1'b0));
  BitSelector #(.width(16)) bitselector_2 (.in(Machine_Code), .out(bitselector_2_out), .sel(4'b1100));
  not not_1 (not_1_out, Flags_In[3]);
  or or_2 (or_2_out, not_1_out, Flags_In[1]);
  BitSelector #(.width(16), .group(4)) bitselector_3 (.in(Machine_Code), .out(bitselector_3_out), .sel(2'b10));
  assign bit_extender_1_out = {{8{bitselector_1_out[7]}}, bitselector_1_out};  // Bit_Extender bit_extender_1
  not not_2 (not_2_out, Halt);
  Adder #(.width(16)) adder_1 (.a(Last_Line), .b({16{1'b0}}), .out(PC_1), .cin(not_2_out));  // open: cout
  not not_3 (not_3_out, xor_1_out);
  not not_4 (not_4_out, or_1_out);
  not not_5 (not_5_out, or_2_out);
  not not_6 (not_6_out, Flags_In[1]);
  not not_7 (not_7_out, Flags_In[3]);
  not not_8 (not_8_out, Flags_In[0]);
  not not_9 (not_9_out, Flags_In[2]);
  Comparator comparator_2 (.a(Machine_Code[15:8]), .b(8'h22), .eq(comparator_2_eq));  // open: gt, lt
  Comparator comparator_3 (.a(Machine_Code[15:8]), .b(8'h29), .eq(comparator_3_eq));  // open: gt, lt
  Adder #(.width(16)) adder_2 (.a(Last_Line), .b(bit_extender_1_out), .out(adder_2_out));  // open: cin, cout
  Multiplexer #(.width(16)) multiplexer_1 (
    .in0(PC_1), .in1(Branch_line), .out(multiplexer_1_out), .sel(multiplexer_2_out));  // open: en
  Multiplexer #(.select(4)) multiplexer_2 (
    .in0(1'b1), .in1(1'b1), .in2(xor_1_out), .in3(not_3_out), .in4(or_1_out), .in5(not_4_out),
    .in6(or_2_out), .in7(not_5_out), .in8(Flags_In[1]), .in9(not_6_out), .in10(Flags_In[3]),
    .in11(not_7_out), .in12(Flags_In[0]), .in13(not_8_out), .in14(Flags_In[2]), .in15(not_9_out),
    .out(multiplexer_2_out), .sel(bitselector_3_out));  // open: en
  Register #(.width(16), .trigger("falling")) register_1 (
    .D(PC_1), .Q(PCforContext), .clk(comparator_2_eq));  // open: en, clr
  Register #(.width(16), .trigger("falling")) register_2 (
    .D(Read_2), .Q(register_2_q), .clk(comparator_3_eq));  // open: en, clr
  Comparator #(.width(7)) comparator_4 (.a(Machine_Code[15:9]), .b(7'b0010000), .eq(Doing_C_R));  // open: gt, lt
  or or_3 (or_3_out, bitselector_2_out, Doing_C_R);
  Comparator #(.width(3)) comparator_5 (
    .a({Machine_Code[13], Machine_Code[14], Machine_Code[15]}), .b(3'b000), .eq(comparator_5_eq));  // open: gt, lt
  Multiplexer #(.width(16)) multiplexer_3 (
    .in0(adder_2_out), .in1(Read_2), .out(Branch_line), .sel(or_3_out));  // open: en
  or or_4 (or_4_out, comparator_5_eq, Doing_C_R);
  Multiplexer #(.width(16)) multiplexer_4 (
    .in0(PC_1), .in1(multiplexer_1_out), .out(multiplexer_4_out), .sel(or_4_out));  // open: en
  Multiplexer #(.width(16)) multiplexer_5 (
    .in0(multiplexer_4_out), .in1(register_2_q), .out(Next_Line), .sel(comparator_6_eq));  // open: en
  Comparator #(.width(16)) comparator_6 (.a(Machine_Code), .b(16'h2300), .eq(comparator_6_eq));  // open: gt, lt

  // Other names for the same wires on the sheet: s_in = Flags_In[0]; z_in = Flags_In[1]; v_in = Flags_In[2];
  //   c_in = Flags_In[3]; cb_in = Flags_In[4]; Read2[15:0] = Read_2

  // Notes on the sheet:
  //   Conditions
  //   For Branching
  //   Determine Line to Which We WOULD Branch
  //   Do we have
  //   a branch op code?
  //   Determine If We Are Branching
  //   Branch Select
  //   Is Branch
  //   Allowed?
  //   Do we have a
  //   call/return op code?
  //   Are We
  //   Branching?
  //   Are we doing
  //   a context switch?
endmodule

module Microprocessor (
  output [4:0] BCVZS
);

  wire CLK, CLR, Flag_Enable, getchar_key1en, getchar_key2en, getchar_mux_select, K1_Av, K2_Av,
       Op_Control_doing_c_r, Op_Control_load, Op_Control_memory_select, Op_Control_register_enable,
       Op_Control_store, or_1_out, putchar_t0_enable, putchar_t1_enable;
  wire [3:0] Op_Control_read_address_1, Op_Control_read_address_2, Op_Control_write_address_1;
  wire [4:0] ALSU_flags_out;
  wire [6:0] keyboard_1_data, keyboard_2_data, Keyboard_Data, putchar_ascii_code;
  wire [15:0] ALSU_data_out, MCode, Next_Line_Counter_next_line, Op_Control_mem_load_read, PC4Con, PC_1,
       ram_1_data, RD1, RD2, RD3, register_1_q, register_file_1_r4_value, register_file_1_r6_value,
       register_file_1_r8_value, rom_1_data;

  Clock clock_1 (.out(CLK));
  Button button_1 (.out(CLR));
  getchar getchar (
    .Machine_Code(MCode), .Read_1(RD1), .Key1En(getchar_key1en), .Key2En(getchar_key2en),
    .Mux_Select(getchar_mux_select));
  Next_Line_Counter Next_Line_Counter (
    .Last_Line(register_1_q), .Machine_Code(MCode), .Read_2(RD2), .Flags_In(BCVZS), .PC_1(PC_1),
    .Next_Line(Next_Line_Counter_next_line), .PCforContext(PC4Con));
  Operation_Control Op_Control (
    .Machine_Code(MCode), .Read_Data_2(RD2), .Read_Address_1(Op_Control_read_address_1),
    .Read_Address_2(Op_Control_read_address_2), .Write_Address_1(Op_Control_write_address_1),
    .register_enable(Op_Control_register_enable), .Doing_C_R(Op_Control_doing_c_r),
    .flag_enable(Flag_Enable), .Memory_Select(Op_Control_memory_select), .Load(Op_Control_load),
    .Store(Op_Control_store), .mem_load_read(Op_Control_mem_load_read));
  Keyboard keyboard_1 (.clk(CLK), .re(getchar_key1en), .clr(CLR), .avail(K1_Av), .data(keyboard_1_data));
  Keyboard keyboard_2 (.clk(CLK), .re(getchar_key2en), .clr(CLR), .avail(K2_Av), .data(keyboard_2_data));
  Register #(.width(16)) register_1 (
    .D(Next_Line_Counter_next_line), .Q(register_1_q), .clk(CLK), .clr(CLR));  // open: en
  Register_File register_file_1 (
    .select(1'b1), .enable(Op_Control_register_enable), .clock(CLK), .Write_Data_1(ALSU_data_out),
    .Write_Data_2__Read_3(RD3), .Write_Data_3__Read_1(RD1), .Write_Address_1(Op_Control_write_address_1),
    .Write_Address_2(Op_Control_read_address_1), .Doing_C_R(Op_Control_doing_c_r),
    .Read_Address_1(Op_Control_read_address_1), .Read_Address_2(Op_Control_read_address_2),
    .R4_value(register_file_1_r4_value), .R6_value(register_file_1_r6_value),
    .R8_value(register_file_1_r8_value), .reset(CLR), .read_data_1(RD1), .read_data_2(RD2), .read_data_3(RD3));
  RAM #(.addrWidth(16), .dataWidth(16), .bus("separate")) ram_1 (
    .addr(Op_Control_mem_load_read), .din(RD1), .data(ram_1_data), .str(Op_Control_store),
    .sel(Op_Control_memory_select), .clk(CLK), .ld(Op_Control_load), .clr(CLR));
  Multiplexer #(.width(7)) multiplexer_1 (
    .in0(keyboard_1_data), .in1(keyboard_2_data), .out(Keyboard_Data), .sel(getchar_mux_select), .en(or_1_out));
  or or_1 (or_1_out, K1_Av, K2_Av);
  ROM #(.addrWidth(16), .dataWidth(16)) rom_1 (.addr(register_1_q), .data(rom_1_data));  // open: sel
  ALSU ALSU (
    .Machine_Code(MCode), .Read_1(RD1), .Read_2(RD2), .Flags_In(BCVZS), .Mem_Load(ram_1_data), .PC_1(PC_1),
    .Key1_av(K1_Av), .Key2_av(K2_Av), .Keyboard_In(Keyboard_Data), .PC4Context(PC4Con),
    .Data_Out(ALSU_data_out), .Flags_Out(ALSU_flags_out));
  Interrupt_Handler Interrupt (
    .Machine_Code(rom_1_data), .key1_av(K1_Av), .in_infinite_loop(register_1_q), .key2_av(K2_Av),
    .R4_value(register_file_1_r4_value), .R6_value(register_file_1_r6_value),
    .R8_value(register_file_1_r8_value), .Machine_Code_2(MCode));
  Flags Flags (.BCVZS_In(ALSU_flags_out), .enable(Flag_Enable), .clock(CLK), .reset(CLR), .BCVZS_Out(BCVZS));
  putchar_ord putchar (
    .Machine_Code(MCode), .Read_1(RD1), .Read_2(RD2), .T0_enable(putchar_t0_enable),
    .T1_enable(putchar_t1_enable), .ASCII_code(putchar_ascii_code));
  TTY tty_1 (.data(putchar_ascii_code), .clk(CLK), .we(putchar_t0_enable), .clr(CLR));
  TTY tty_2 (.data(putchar_ascii_code), .clk(CLK), .we(putchar_t1_enable), .clr(CLR));

  // Other names for the same wires on the sheet: Flags[4:0] = BCVZS

  // Notes on the sheet:
  //   Microprocessor
  //   RAM
  //   ROM
  //   contents of rom_1 (hex, n*v repeats v):
  //   e600 f610 e800 f820 eb04 fb00 e600 f610 e800 f820 e400 f430 2200 100b 4082*0 e300 f300 e404 f400
  //   2534 9240 e100 f100 2412 2056 4086*0 e301 f300 2534 9130 9240 e90a f900 3068 b029 ec1f fc20 190c
  //   620a ea00 fa00 e80a f800 e900 f900 4409 9240 2412 3068 b048 ec21 fc20 180c 3980 ed13 fd20 100d 620a
  //   3a80 2078 4062*0 6100 e100 f150 6221 6331 6441 6551 6661 6771 6881 6991 6aa1 6bb1 6cc1 6dd1 6ee1
  //   6ff1 2802 6201 3270 7201 e100 f140 5201 3278 4201 2902 4221 4331 4441 4551 4661 4771 4881 4991 4aa1
  //   4bb1 4cc1 4dd1 4ee1 4ff1 4111 6100 6210 6320 e100 f140 e200 f250 4302 6301 4312 6311 4322 6321 4322
  //   6321 4332 6331 4342 6341 4352 6351 4362 6361 4372 6371 4382 6381 4392 6391 43a2 63a1 43b2 63b1 43c2
  //   63c1 43d2 63d1 43e2 63e1 43f2 63f1 5302 7301 4100 4210 4320 2300 4008*0 1 2 3 4 5 6 7 8 9 a b c d e
  //   f
  //   values of specific registers
  //   4, 6, and 8
endmodule

module Flags (
  input  [4:0] BCVZS_In,
  input  enable,
  input  clock,
  input  reset,
  output [4:0] BCVZS_Out
);

  Register #(.width(5)) register_1 (.D(BCVZS_In), .en(enable), .Q(BCVZS_Out), .clk(clock), .clr(reset));
endmodule

module ALSU (
  input  [15:0] Machine_Code,
  input  [15:0] Read_1,
  input  [15:0] Read_2,
  input  [4:0] Flags_In,
  input  [15:0] Mem_Load,
  input  [15:0] PC_1,
  input  Key1_av,
  input  Key2_av,
  input  [6:0] Keyboard_In,
  input  [15:0] PC4Context,
  output [15:0] Data_Out,
  output [4:0] Flags_Out
);

  wire Bit_3, or_1_out;
  wire [1:0] Bits_11_10, memflags;
  wire [3:0] I_O_Select, Op_Select, Shift_Select;
  wire [4:0] add_add_flags_out, and_and_flags_out, asl_asl_flag_out, asr_asr_flag_out, dec_dec_flags_out,
       FOFF, FON, FSET4, FSET5, inc_inc_flags_out, lsl8_lsl8_flag_out, lsl_lsr_flag_out, lsr8_lsr8_flag_out,
       lsr_lsr_flag_out, mult_mult_flags_out, multiplexer_2_out, multiplexer_3_out, multiplexer_6_out,
       or_2_or_flags_out, RSTRF, subtract_subtract_flags_out, xor_xor_flags_out;
  wire [15:0] add_add_data_out, and_and_data_out, asl_asl_data_out, asr_asr_data_out, bit_extender_2_out,
       dec_dec_data_out, inc_inc_data_out, Keyboard_Data, lsl8_lsl8_data_out, lsl_lsr_data_out,
       lsr8_lsr8_data_out, lsr_lsr_data_out, mult_mult_data_out, multiplexer_4_out, multiplexer_5_out,
       multiplexer_7_out, or_2_or_data_out, PC_1_t, sethi_sethi_data_out, setlo_setlo_data_out,
       subtract_subtract_data_out, subtractor_1_out, xor_xor_data_out;

  BitSelector #(.width(16), .group(2)) bitselector_1 (.in(Machine_Code), .out(Bits_11_10), .sel(3'b101));
  assign Keyboard_Data = {{9{1'b0}}, Keyboard_In};  // Bit_Extender bit_extender_1
  BitSelector #(.width(16)) bitselector_2 (.in(Machine_Code), .out(Bit_3), .sel(4'b0011));
  BitSelector #(.width(16)) bitselector_3 (.in(Mem_Load), .out(memflags[0]), .sel(4'b1111));
  Comparator #(.width(16), .mode("unsigned")) comparator_1 (
    .a(Mem_Load), .b({16{1'b0}}), .eq(memflags[1]));  // open: gt, lt
  Subtractor #(.width(16)) subtractor_1 (.a(PC_1), .b(16'h1), .out(subtractor_1_out));  // open: bin, bout
  or or_1 (or_1_out, Key1_av, Key2_av);
  BitSelector #(.width(16), .group(4)) bitselector_4 (.in(Machine_Code), .out(Op_Select), .sel(2'b11));
  Multiplexer #(.width(16)) multiplexer_1 (
    .in0(PC_1), .in1(subtractor_1_out), .out(PC_1_t), .sel(or_1_out));  // open: en
  BitSelector #(.width(16), .group(4)) bitselector_5 (.in(Machine_Code), .out(Shift_Select), .sel(2'b01));
  BitSelector #(.width(16), .group(4)) bitselector_6 (.in(Machine_Code), .out(I_O_Select), .sel(2'b10));
  flag_operations Flag_Operations (
    .Read_1(Read_1), .Machine_Code(Machine_Code), .Flags_In(Flags_In), .RSTRF(RSTRF), .FSETON(FON),
    .FSETOFF(FOFF), .FSET5(FSET5), .FSET4(FSET4));
  increment inc (
    .Flags_In(Flags_In), .Read_1(Read_1), .Machine_Code(Machine_Code), .INC_Data_Out(inc_inc_data_out),
    .INC_Flags_Out(inc_inc_flags_out));
  decrement dec (
    .Flags_In(Flags_In), .Read_1(Read_1), .Machine_Code(Machine_Code), .DEC_Data_Out(dec_dec_data_out),
    .DEC_Flags_Out(dec_dec_flags_out));
  lsl lsl (.Read_2(Read_2), .Flags_In(Flags_In), .LSR_Data_Out(lsl_lsr_data_out), .LSR_Flag_Out(lsl_lsr_flag_out));
  lsr lsr (.Read_2(Read_2), .Flags_In(Flags_In), .LSR_Data_Out(lsr_lsr_data_out), .LSR_Flag_Out(lsr_lsr_flag_out));
  lsl8 lsl8 (
    .Read_2(Read_2), .Flags_In(Flags_In), .LSL8_Data_Out(lsl8_lsl8_data_out),
    .LSL8_Flag_Out(lsl8_lsl8_flag_out));
  lsr8 lsr8 (
    .Read_2(Read_2), .Flags_In(Flags_In), .LSR8_Data_Out(lsr8_lsr8_data_out),
    .LSR8_Flag_Out(lsr8_lsr8_flag_out));
  asl asl (.Read_2(Read_2), .Flags_In(Flags_In), .ASL_Data_Out(asl_asl_data_out), .ASL_Flag_Out(asl_asl_flag_out));
  asr asr (.Read_2(Read_2), .Flags_In(Flags_In), .ASR_Data_Out(asr_asr_data_out), .ASR_Flag_Out(asr_asr_flag_out));
  \and  \and  (
    .Read_1(Read_1), .Read_2(Read_2), .Flags_In(Flags_In), .AND_Data_Out(and_and_data_out),
    .AND_Flags_Out(and_and_flags_out));
  \or  or_2 (
    .Read_1(Read_1), .Read_2(Read_2), .Flags_In(Flags_In), .OR_Data_Out(or_2_or_data_out),
    .OR_Flags_Out(or_2_or_flags_out));
  add add (
    .Flags_In(Flags_In), .Read_1(Read_1), .Read_2(Read_2), .ADD_Data_Out(add_add_data_out),
    .ADD_Flags_Out(add_add_flags_out));
  subtract subtract (
    .Flags_In(Flags_In), .Read_1(Read_1), .Read_2(Read_2), .SUBTRACT_Data_Out(subtract_subtract_data_out),
    .SUBTRACT_Flags_Out(subtract_subtract_flags_out));
  multiplication mult (
    .Read_1(Read_1), .Read_2(Read_2), .Flags_In(Flags_In), .MULT_Data_Out(mult_mult_data_out),
    .MULT_Flags_Out(mult_mult_flags_out));
  \xor  \xor  (
    .Read_1(Read_1), .Read_2(Read_2), .Flags_In(Flags_In), .XOR_Data_Out(xor_xor_data_out),
    .XOR_Flags_Out(xor_xor_flags_out));
  setlo setlo (.Machine_Code(Machine_Code), .SETLO_Data_Out(setlo_setlo_data_out));
  sethi sethi (.Read_1(Read_1), .Machine_Code(Machine_Code), .SETHI_Data_Out(sethi_sethi_data_out));
  Multiplexer #(.width(5)) multiplexer_2 (
    .in0(Flags_In), .in1(RSTRF), .out(multiplexer_2_out), .sel(Bit_3));  // open: en
  Multiplexer #(.select(2), .width(5)) multiplexer_3 (
    .in0(FON), .in1(FSET5), .in2(FOFF), .in3(FSET4), .out(multiplexer_3_out), .sel(Bits_11_10));  // open: en
  assign bit_extender_2_out = {{11{1'b0}}, Flags_In};  // Bit_Extender bit_extender_2
  Multiplexer #(.width(16)) multiplexer_4 (
    .in0(bit_extender_2_out), .out(multiplexer_4_out), .sel(Bit_3));  // open: in1, en
  Multiplexer #(.select(4), .width(16)) multiplexer_5 (
    .in0(lsl_lsr_data_out), .in1(lsr_lsr_data_out), .in2(lsl8_lsl8_data_out), .in3(lsr8_lsr8_data_out),
    .in4(asl_asl_data_out), .in5(asr_asr_data_out), .in7(multiplexer_4_out), .in8(inc_inc_data_out),
    .in9(inc_inc_data_out), .in10(inc_inc_data_out), .in11(inc_inc_data_out), .in12(dec_dec_data_out),
    .in13(dec_dec_data_out), .in14(dec_dec_data_out), .in15(dec_dec_data_out), .out(multiplexer_5_out),
    .sel(Shift_Select));  // open: in6, en
  Multiplexer #(.select(4), .width(5)) multiplexer_6 (
    .in0(lsl_lsr_flag_out), .in1(lsr_lsr_flag_out), .in2(lsl8_lsl8_flag_out), .in3(lsr8_lsr8_flag_out),
    .in4(asl_asl_flag_out), .in5(asr_asr_flag_out), .in6(multiplexer_3_out), .in7(multiplexer_2_out),
    .in8(inc_inc_flags_out), .in9(inc_inc_flags_out), .in10(inc_inc_flags_out), .in11(inc_inc_flags_out),
    .in12(dec_dec_flags_out), .in13(dec_dec_flags_out), .in14(dec_dec_flags_out), .in15(dec_dec_flags_out),
    .out(multiplexer_6_out), .sel(Shift_Select));  // open: en
  Multiplexer #(.select(4), .width(16)) multiplexer_7 (
    .in0(PC_1_t), .in1(PC_1_t), .in5(Keyboard_Data), .in8(PC4Context), .out(multiplexer_7_out),
    .sel(I_O_Select));  // open: in2, in3, in4, in6, in7, in9, in10, in11, in12, in13, in14, in15, en
  Multiplexer #(.select(4), .width(16)) multiplexer_8 (
    .in2(multiplexer_7_out), .in3(multiplexer_5_out), .in4(Mem_Load), .in5(Mem_Load), .in8(and_and_data_out),
    .in9(or_2_or_data_out), .in10(add_add_data_out), .in11(subtract_subtract_data_out),
    .in12(mult_mult_data_out), .in13(xor_xor_data_out), .in14(setlo_setlo_data_out),
    .in15(sethi_sethi_data_out), .out(Data_Out), .sel(Op_Select));  // open: in0, in1, in6, in7, en
  Multiplexer #(.select(4), .width(5)) multiplexer_9 (
    .in3(multiplexer_6_out), .in4({Flags_In[4:2], memflags}), .in5({Flags_In[4:2], memflags}),
    .in8(and_and_flags_out), .in9(or_2_or_flags_out), .in10(add_add_flags_out),
    .in11(subtract_subtract_flags_out), .in12(mult_mult_flags_out), .in13(xor_xor_flags_out),
    .in14(Flags_In), .in15(Flags_In), .out(Flags_Out), .sel(Op_Select));  // open: in0, in1, in2, in6, in7, en

  // Other names for the same wires on the sheet: F_IN[4:0] = Flags_In; MCode[15:0] = Machine_Code;
  //   memdata[15:0] = Mem_Load; memflags[4:2] = Flags_In[4:2]; RD1[15:0] = Read_1; RD2[15:0] = Read_2

  // Notes on the sheet:
  //   shift multiplexer
  //   shift multiplexer
  //   I/O
  //   overall multiplexer
  //   overall multiplexer
endmodule

module setlo (
  input  [15:0] Machine_Code,
  output [15:0] SETLO_Data_Out
);

  wire [7:0] bitselector_1_out;

  BitSelector #(.width(16), .group(8)) bitselector_1 (.in(Machine_Code), .out(bitselector_1_out), .sel(1'b0));
  assign SETLO_Data_Out = {{8{bitselector_1_out[7]}}, bitselector_1_out};  // Bit_Extender bit_extender_1
endmodule

module sethi (
  input  [15:0] Read_1,
  input  [15:0] Machine_Code,
  output [15:0] SETHI_Data_Out
);

  BitSelector #(.width(16), .group(8)) bitselector_1 (.in(Read_1), .out(SETHI_Data_Out[7:0]), .sel(1'b0));
  BitSelector #(.width(16), .group(8)) bitselector_2 (.in(Machine_Code), .out(SETHI_Data_Out[15:8]), .sel(1'b0));
endmodule

module \and  (
  input  [15:0] Read_1,
  input  [15:0] Read_2,
  input  [4:0] Flags_In,
  output [15:0] AND_Data_Out,
  output [4:0] AND_Flags_Out
);

  assign AND_Data_Out = Read_1 & Read_2;  // AND_Gate AND, 16 bits wide
  BitSelector #(.width(16)) bitselector_1 (.in(AND_Data_Out), .out(AND_Flags_Out[0]), .sel(4'b1111));
  Comparator #(.width(16), .mode("unsigned")) comparator_1 (
    .a(AND_Data_Out), .b({16{1'b0}}), .eq(AND_Flags_Out[1]));  // open: gt, lt

  assign AND_Flags_Out[4:2] = Flags_In[4:2];
endmodule

module \or  (
  input  [15:0] Read_1,
  input  [15:0] Read_2,
  input  [4:0] Flags_In,
  output [15:0] OR_Data_Out,
  output [4:0] OR_Flags_Out
);

  assign OR_Data_Out = Read_1 | Read_2;  // OR_Gate OR, 16 bits wide
  BitSelector #(.width(16)) bitselector_1 (.in(OR_Data_Out), .out(OR_Flags_Out[0]), .sel(4'b1111));
  Comparator #(.width(16), .mode("unsigned")) comparator_1 (
    .a(OR_Data_Out), .b({16{1'b0}}), .eq(OR_Flags_Out[1]));  // open: gt, lt

  assign OR_Flags_Out[4:2] = Flags_In[4:2];
endmodule

module \xor  (
  input  [15:0] Read_1,
  input  [15:0] Read_2,
  input  [4:0] Flags_In,
  output [15:0] XOR_Data_Out,
  output [4:0] XOR_Flags_Out
);

  assign XOR_Data_Out = Read_1 ^ Read_2;  // XOR_Gate XOR, 16 bits wide
  BitSelector #(.width(16)) bitselector_1 (.in(XOR_Data_Out), .out(XOR_Flags_Out[0]), .sel(4'b1111));
  Comparator #(.width(16), .mode("unsigned")) comparator_1 (
    .a(XOR_Data_Out), .b({16{1'b0}}), .eq(XOR_Flags_Out[1]));  // open: gt, lt

  assign XOR_Flags_Out[4:2] = Flags_In[4:2];
endmodule

module add (
  input  [4:0] Flags_In,
  input  [15:0] Read_1,
  input  [15:0] Read_2,
  output [15:0] ADD_Data_Out,
  output [4:0] ADD_Flags_Out
);

  wire and_1_out, bitselector_1_out, bitselector_2_out, not_1_out;

  not not_1 (not_1_out, Flags_In[4]);
  and and_1 (and_1_out, Flags_In[3], not_1_out);
  BitSelector #(.width(16)) bitselector_1 (.in(Read_1), .out(bitselector_1_out), .sel(4'b1111));
  BitSelector #(.width(16)) bitselector_2 (.in(Read_2), .out(bitselector_2_out), .sel(4'b1111));
  Adder #(.width(16)) adder_1 (.a(Read_1), .b(Read_2), .out(ADD_Data_Out), .cin(and_1_out), .cout(ADD_Flags_Out[3]));
  BitSelector #(.width(16)) bitselector_3 (.in(ADD_Data_Out), .out(ADD_Flags_Out[0]), .sel(4'b1111));
  Comparator #(.width(16), .mode("unsigned")) comparator_1 (
    .a(ADD_Data_Out), .b({16{1'b0}}), .eq(ADD_Flags_Out[1]));  // open: gt, lt
  add_overflow_detect AOD (
    .Result_Bit(ADD_Flags_Out[0]), .Input_Bit_1(bitselector_1_out), .Input_Bit_2(bitselector_2_out),
    .Overflow(ADD_Flags_Out[2]));

  assign ADD_Flags_Out[4] = Flags_In[4];
endmodule

module add_overflow_detect (
  input  Result_Bit,
  input  Input_Bit_1,
  input  Input_Bit_2,
  output Overflow
);

  wire and_1_out, and_2_out, and_3_out, and_4_out, not_1_out, not_2_out, not_3_out;

  not not_1 (not_1_out, Input_Bit_2);
  not not_2 (not_2_out, Input_Bit_1);
  and and_1 (and_1_out, not_2_out, not_1_out);
  not not_3 (not_3_out, Result_Bit);
  and and_2 (and_2_out, Input_Bit_1, Input_Bit_2);
  and and_3 (and_3_out, Result_Bit, and_1_out);
  and and_4 (and_4_out, not_3_out, and_2_out);
  or or_1 (Overflow, and_3_out, and_4_out);

  // Notes on the sheet:
  //   low-bit to low-bit addition
  //   high-bit to high-bit addition
  //   high-bit output
  //   low-bit output
endmodule

module subtract (
  input  [4:0] Flags_In,
  input  [15:0] Read_1,
  input  [15:0] Read_2,
  output [15:0] SUBTRACT_Data_Out,
  output [4:0] SUBTRACT_Flags_Out
);

  wire and_1_out, bitselector_1_out, bitselector_2_out, not_1_out, not_2_out, subtractor_1_bout;

  not not_1 (not_1_out, Flags_In[3]);
  not not_2 (not_2_out, Flags_In[4]);
  and and_1 (and_1_out, not_1_out, not_2_out);
  not not_3 (SUBTRACT_Flags_Out[3], subtractor_1_bout);
  BitSelector #(.width(16)) bitselector_1 (.in(Read_1), .out(bitselector_1_out), .sel(4'b1111));
  BitSelector #(.width(16)) bitselector_2 (.in(Read_2), .out(bitselector_2_out), .sel(4'b1111));
  Subtractor #(.width(16)) subtractor_1 (
    .a(Read_1), .b(Read_2), .out(SUBTRACT_Data_Out), .bin(and_1_out), .bout(subtractor_1_bout));
  BitSelector #(.width(16)) bitselector_3 (.in(SUBTRACT_Data_Out), .out(SUBTRACT_Flags_Out[0]), .sel(4'b1111));
  Comparator #(.width(16), .mode("unsigned")) comparator_1 (
    .a(SUBTRACT_Data_Out), .b({16{1'b0}}), .eq(SUBTRACT_Flags_Out[1]));  // open: gt, lt
  subtract_overflow_detect SOD (
    .Result_Bit(SUBTRACT_Flags_Out[0]), .Minuend_Bit(bitselector_1_out), .Subtrahend_Bit(bitselector_2_out),
    .Overflow(SUBTRACT_Flags_Out[2]));

  assign SUBTRACT_Flags_Out[4] = Flags_In[4];
endmodule

module subtract_overflow_detect (
  input  Result_Bit,
  input  Minuend_Bit,
  input  Subtrahend_Bit,
  output Overflow
);

  wire and_1_out, and_2_out, not_1_out, not_2_out, not_3_out;

  not not_1 (not_1_out, Minuend_Bit);
  not not_2 (not_2_out, Result_Bit);
  not not_3 (not_3_out, Subtrahend_Bit);
  and and_1 (and_1_out, not_1_out, Subtrahend_Bit, Result_Bit);
  and and_2 (and_2_out, not_2_out, not_3_out, Minuend_Bit);
  or or_1 (Overflow, and_1_out, and_2_out);
endmodule

module multiplication (
  input  [15:0] Read_1,
  input  [15:0] Read_2,
  input  [4:0] Flags_In,
  output [15:0] MULT_Data_Out,
  output [4:0] MULT_Flags_Out
);

  wire and_1_out, comparator_1_eq, comparator_2_eq, comparator_4_eq, not_1_out, not_2_out, not_3_out,
       not_4_out, or_1_out;
  wire [15:0] bitselector_1_out, bitselector_2_out, bitselector_3_out;
  wire [31:0] bit_extender_1_out, bit_extender_2_out, bit_extender_3_out, bit_extender_4_out,
       multiplier_1_out, multiplier_2_out;

  not not_1 (not_1_out, Flags_In[1]);
  not not_2 (not_2_out, Flags_In[2]);
  not not_3 (not_3_out, Flags_In[3]);
  not not_4 (not_4_out, Flags_In[4]);
  and and_1 (and_1_out, Flags_In[0], not_1_out, not_2_out, not_3_out, not_4_out);
  assign bit_extender_1_out = {{16{1'b0}}, Read_1};  // Bit_Extender bit_extender_1
  assign bit_extender_2_out = {{16{1'b0}}, Read_2};  // Bit_Extender bit_extender_2
  assign bit_extender_3_out = {{16{Read_1[15]}}, Read_1};  // Bit_Extender bit_extender_3
  assign bit_extender_4_out = {{16{Read_2[15]}}, Read_2};  // Bit_Extender bit_extender_4
  Multiplier #(.width(32)) multiplier_1 (
    .a(bit_extender_3_out), .b(bit_extender_4_out), .out(multiplier_1_out));  // open: cin, cout
  BitSelector #(.width(32), .group(16)) bitselector_1 (.in(multiplier_2_out), .out(bitselector_1_out), .sel(1'b0));
  Multiplier #(.width(32)) multiplier_2 (
    .a(bit_extender_1_out), .b(bit_extender_2_out), .out(multiplier_2_out));  // open: cin, cout
  BitSelector #(.width(32), .group(16)) bitselector_2 (.in(multiplier_2_out), .out(bitselector_2_out), .sel(1'b1));
  BitSelector #(.width(32), .group(16)) bitselector_3 (.in(multiplier_1_out), .out(bitselector_3_out), .sel(1'b1));
  Multiplexer #(.width(16)) multiplexer_1 (
    .in0(bitselector_1_out), .in1(bitselector_3_out), .out(MULT_Data_Out), .sel(and_1_out));  // open: en
  Comparator #(.width(16)) comparator_1 (.a(bitselector_3_out), .b({16{1'b0}}), .eq(comparator_1_eq));  // open: gt, lt
  Comparator #(.width(16)) comparator_2 (.a(bitselector_3_out), .b({16{1'b1}}), .eq(comparator_2_eq));  // open: gt, lt
  Comparator #(.width(16), .mode("unsigned")) comparator_3 (
    .a(MULT_Data_Out), .b({16{1'b0}}), .eq(MULT_Flags_Out[1]));  // open: gt, lt
  Comparator #(.width(16), .mode("unsigned")) comparator_4 (
    .a(bitselector_2_out), .b({16{1'b0}}), .eq(comparator_4_eq));  // open: gt, lt
  or or_1 (or_1_out, comparator_1_eq, comparator_2_eq);
  BitSelector #(.width(16)) bitselector_4 (.in(MULT_Data_Out), .out(MULT_Flags_Out[0]), .sel(4'b1111));
  not not_5 (MULT_Flags_Out[3], comparator_4_eq);
  not not_6 (MULT_Flags_Out[2], or_1_out);

  assign MULT_Flags_Out[4] = Flags_In[4];

  // Notes on the sheet:
  //   Sign Flag
  //   Other Flags
  //   MULTIPLICATION
  //   INCREMENT
  //   low bits
  //   high bits
  //   high bits
endmodule

module increment (
  input  [4:0] Flags_In,
  input  [15:0] Read_1,
  input  [15:0] Machine_Code,
  output [15:0] INC_Data_Out,
  output [4:0] INC_Flags_Out
);

  wire bitselector_1_out, bitselector_2_out;
  wire [15:0] adder_1_out, bit_extender_1_out;

  assign bit_extender_1_out = {{10{1'b0}}, Machine_Code[5:0]};  // Bit_Extender bit_extender_1
  Adder #(.width(16)) adder_1 (.a(bit_extender_1_out), .b(16'h1), .out(adder_1_out));  // open: cin, cout
  BitSelector #(.width(16)) bitselector_1 (.in(Read_1), .out(bitselector_1_out), .sel(4'b1111));
  BitSelector #(.width(16)) bitselector_2 (.in(adder_1_out), .out(bitselector_2_out), .sel(4'b1111));
  Adder #(.width(16)) adder_2 (.a(Read_1), .b(adder_1_out), .out(INC_Data_Out), .cout(INC_Flags_Out[3]));  // open: cin
  BitSelector #(.width(16)) bitselector_3 (.in(INC_Data_Out), .out(INC_Flags_Out[0]), .sel(4'b1111));
  Comparator #(.width(16), .mode("unsigned")) comparator_1 (
    .a(INC_Data_Out), .b({16{1'b0}}), .eq(INC_Flags_Out[1]));  // open: gt, lt
  add_overflow_detect AOD (
    .Result_Bit(INC_Flags_Out[0]), .Input_Bit_1(bitselector_1_out), .Input_Bit_2(bitselector_2_out),
    .Overflow(INC_Flags_Out[2]));

  assign INC_Flags_Out[4] = Flags_In[4];
endmodule

module decrement (
  input  [4:0] Flags_In,
  input  [15:0] Read_1,
  input  [15:0] Machine_Code,
  output [15:0] DEC_Data_Out,
  output [4:0] DEC_Flags_Out
);

  wire bitselector_1_out, bitselector_2_out, subtractor_1_bout;
  wire [15:0] adder_1_out, bit_extender_1_out;

  assign bit_extender_1_out = {{10{1'b0}}, Machine_Code[5:0]};  // Bit_Extender bit_extender_1
  Adder #(.width(16)) adder_1 (.a(bit_extender_1_out), .b(16'h1), .out(adder_1_out));  // open: cin, cout
  not not_1 (DEC_Flags_Out[3], subtractor_1_bout);
  BitSelector #(.width(16)) bitselector_1 (.in(Read_1), .out(bitselector_1_out), .sel(4'b1111));
  BitSelector #(.width(16)) bitselector_2 (.in(adder_1_out), .out(bitselector_2_out), .sel(4'b1111));
  Subtractor #(.width(16)) subtractor_1 (
    .a(Read_1), .b(adder_1_out), .out(DEC_Data_Out), .bout(subtractor_1_bout));  // open: bin
  BitSelector #(.width(16)) bitselector_3 (.in(DEC_Data_Out), .out(DEC_Flags_Out[0]), .sel(4'b1111));
  Comparator #(.width(16), .mode("unsigned")) comparator_1 (
    .a(DEC_Data_Out), .b({16{1'b0}}), .eq(DEC_Flags_Out[1]));  // open: gt, lt
  subtract_overflow_detect SOD (
    .Result_Bit(DEC_Flags_Out[0]), .Minuend_Bit(bitselector_1_out), .Subtrahend_Bit(bitselector_2_out),
    .Overflow(DEC_Flags_Out[2]));

  assign DEC_Flags_Out[4] = Flags_In[4];
endmodule

module lsr (
  input  [15:0] Read_2,
  input  [4:0] Flags_In,
  output [15:0] LSR_Data_Out,
  output [4:0] LSR_Flag_Out
);

  wire and_1_out, not_1_out;
  wire [15:0] or_1_out, shifter_1_out, shifter_2_out;

  Shifter #(.width(16), .shift("lr")) shifter_1 (.in(Read_2), .\dist (4'b0001), .out(shifter_1_out));
  Shifter #(.width(16), .shift("lr")) shifter_2 (.in(Read_2), .\dist (4'b0001), .out(shifter_2_out));
  not not_1 (not_1_out, Flags_In[4]);
  assign or_1_out = shifter_2_out | 16'h8000;  // OR_Gate or_1, 16 bits wide
  and and_1 (and_1_out, Flags_In[3], not_1_out);
  Multiplexer #(.width(16)) multiplexer_1 (
    .in0(shifter_1_out), .in1(or_1_out), .out(LSR_Data_Out), .sel(and_1_out));  // open: en
  BitSelector #(.width(16)) bitselector_1 (.in(Read_2), .out(LSR_Flag_Out[3]), .sel(4'b0000));
  BitSelector #(.width(16)) bitselector_2 (.in(LSR_Data_Out), .out(LSR_Flag_Out[0]), .sel(4'b1111));
  Comparator #(.width(16), .mode("unsigned")) comparator_1 (
    .a(LSR_Data_Out), .b({16{1'b0}}), .eq(LSR_Flag_Out[1]));  // open: gt, lt

  assign {LSR_Flag_Out[4], LSR_Flag_Out[2]} = {Flags_In[4], Flags_In[2]};

  // Notes on the sheet:
  //   LSR
endmodule

module lsl (
  input  [15:0] Read_2,
  input  [4:0] Flags_In,
  output [15:0] LSR_Data_Out,
  output [4:0] LSR_Flag_Out
);

  wire and_1_out, not_1_out;
  wire [15:0] adder_1_out, shifter_1_out, shifter_2_out;

  Shifter #(.width(16)) shifter_1 (.in(Read_2), .\dist (4'b0001), .out(shifter_1_out));
  Shifter #(.width(16)) shifter_2 (.in(Read_2), .\dist (4'b0001), .out(shifter_2_out));
  not not_1 (not_1_out, Flags_In[4]);
  Adder #(.width(16)) adder_1 (.a(shifter_2_out), .b(16'h1), .out(adder_1_out));  // open: cin, cout
  and and_1 (and_1_out, Flags_In[3], not_1_out);
  Multiplexer #(.width(16)) multiplexer_1 (
    .in0(shifter_1_out), .in1(adder_1_out), .out(LSR_Data_Out), .sel(and_1_out));  // open: en
  BitSelector #(.width(16)) bitselector_1 (.in(Read_2), .out(LSR_Flag_Out[3]), .sel(4'b0000));
  BitSelector #(.width(16)) bitselector_2 (.in(LSR_Data_Out), .out(LSR_Flag_Out[0]), .sel(4'b1111));
  Comparator #(.width(16), .mode("unsigned")) comparator_1 (
    .a(LSR_Data_Out), .b({16{1'b0}}), .eq(LSR_Flag_Out[1]));  // open: gt, lt

  assign {LSR_Flag_Out[4], LSR_Flag_Out[2]} = {Flags_In[4], Flags_In[2]};

  // Notes on the sheet:
  //   LSR
endmodule

module lsr8 (
  input  [15:0] Read_2,
  input  [4:0] Flags_In,
  output [15:0] LSR8_Data_Out,
  output [4:0] LSR8_Flag_Out
);

  BitSelector #(.width(16), .group(8)) bitselector_1 (.in(Read_2), .out(LSR8_Data_Out[7:0]), .sel(1'b1));
  BitSelector #(.width(16)) bitselector_2 (.in({{8{1'b0}}, LSR8_Data_Out[7:0]}), .out(LSR8_Flag_Out[0]), .sel(4'b1111));
  Comparator #(.width(16), .mode("unsigned")) comparator_1 (
    .a({{8{1'b0}}, LSR8_Data_Out[7:0]}), .b({16{1'b0}}), .eq(LSR8_Flag_Out[1]));  // open: gt, lt

  assign LSR8_Data_Out[15:8] = {8{1'b0}};
  assign LSR8_Flag_Out[4:2] = Flags_In[4:2];
endmodule

module lsl8 (
  input  [15:0] Read_2,
  input  [4:0] Flags_In,
  output [15:0] LSL8_Data_Out,
  output [4:0] LSL8_Flag_Out
);

  BitSelector #(.width(16), .group(8)) bitselector_1 (.in(Read_2), .out(LSL8_Data_Out[15:8]), .sel(1'b0));
  BitSelector #(.width(16)) bitselector_2 (
    .in({LSL8_Data_Out[15:8], {8{1'b0}}}), .out(LSL8_Flag_Out[0]), .sel(4'b1111));
  Comparator #(.width(16), .mode("unsigned")) comparator_1 (
    .a({LSL8_Data_Out[15:8], {8{1'b0}}}), .b({16{1'b0}}), .eq(LSL8_Flag_Out[1]));  // open: gt, lt

  assign LSL8_Data_Out[7:0] = {8{1'b0}};
  assign LSL8_Flag_Out[4:2] = Flags_In[4:2];
endmodule

module asr (
  input  [15:0] Read_2,
  input  [4:0] Flags_In,
  output [15:0] ASR_Data_Out,
  output [4:0] ASR_Flag_Out
);

  Shifter #(.width(16), .shift("ar")) shifter_1 (.in(Read_2), .\dist (4'b0001), .out(ASR_Data_Out));
  BitSelector #(.width(16)) bitselector_1 (.in(Read_2), .out(ASR_Flag_Out[3]), .sel(4'b0000));
  BitSelector #(.width(16)) bitselector_2 (.in(ASR_Data_Out), .out(ASR_Flag_Out[0]), .sel(4'b1111));
  Comparator #(.width(16), .mode("unsigned")) comparator_1 (
    .a(ASR_Data_Out), .b({16{1'b0}}), .eq(ASR_Flag_Out[1]));  // open: gt, lt

  assign {ASR_Flag_Out[4], ASR_Flag_Out[2]} = {Flags_In[4], Flags_In[2]};

  // Notes on the sheet:
  //   ASR
endmodule

module asl (
  input  [15:0] Read_2,
  input  [4:0] Flags_In,
  output [15:0] ASL_Data_Out,
  output [4:0] ASL_Flag_Out
);

  wire and_1_out, bitselector_1_out, bitselector_2_out, not_1_out;
  wire [15:0] adder_1_out, adder_2_out, shifter_1_out, shifter_2_out;

  BitSelector #(.width(16)) bitselector_1 (.in(Read_2), .out(bitselector_1_out), .sel(4'b1111));
  Shifter #(.width(16)) shifter_1 (.in(Read_2), .\dist (4'b0001), .out(shifter_1_out));
  Shifter #(.width(16)) shifter_2 (.in(Read_2), .\dist (4'b0001), .out(shifter_2_out));
  Adder #(.width(16)) adder_1 (.a(shifter_2_out), .b(16'h1), .out(adder_1_out));  // open: cin, cout
  and and_1 (and_1_out, Flags_In[3], not_1_out);
  not not_1 (not_1_out, Flags_In[4]);
  Adder #(.width(16)) adder_2 (.a(Read_2), .b(Read_2), .out(adder_2_out), .cin(and_1_out));  // open: cout
  BitSelector #(.width(16)) bitselector_2 (.in(adder_2_out), .out(bitselector_2_out), .sel(4'b1111));
  Multiplexer #(.width(16)) multiplexer_1 (
    .in0(shifter_1_out), .in1(adder_1_out), .out(ASL_Data_Out), .sel(and_1_out));  // open: en
  add_overflow_detect AOD (
    .Result_Bit(bitselector_2_out), .Input_Bit_1(bitselector_1_out), .Input_Bit_2(bitselector_1_out),
    .Overflow(ASL_Flag_Out[2]));
  BitSelector #(.width(16)) bitselector_3 (.in(ASL_Data_Out), .out(ASL_Flag_Out[0]), .sel(4'b1111));
  BitSelector #(.width(16)) bitselector_4 (.in(Read_2), .out(ASL_Flag_Out[3]), .sel(4'b1111));
  Comparator #(.width(16), .mode("unsigned")) comparator_1 (
    .a(ASL_Data_Out), .b({16{1'b0}}), .eq(ASL_Flag_Out[1]));  // open: gt, lt

  assign ASL_Flag_Out[4] = Flags_In[4];
endmodule

module flag_operations (
  input  [15:0] Read_1,
  input  [15:0] Machine_Code,
  input  [4:0] Flags_In,
  output [4:0] RSTRF,
  output [4:0] FSETON,
  output [4:0] FSETOFF,
  output [4:0] FSET5,
  output [4:0] FSET4
);

  wire [4:0] not_1_out;

  assign not_1_out = ~{Machine_Code[8], Machine_Code[3:0]};  // NOT_Gate not_1, 5 bits wide
  assign FSETON = {Machine_Code[8], Machine_Code[3:0]} | Flags_In;  // OR_Gate or_1, 5 bits wide
  assign FSETOFF = not_1_out & Flags_In;  // AND_Gate and_1, 5 bits wide

  assign FSET4 = {Flags_In[4], Machine_Code[3:0]};
  assign FSET5 = {Machine_Code[8], Machine_Code[3:0]};
  assign RSTRF = Read_1[4:0];
endmodule

module Operation_Control (
  input  [15:0] Machine_Code,
  input  [15:0] Read_Data_2,
  output [3:0] Read_Address_1,
  output [3:0] Read_Address_2,
  output [3:0] Write_Address_1,
  output register_enable,
  output Doing_C_R,
  output flag_enable,
  output Memory_Select,
  output Load,
  output Store,
  output [15:0] mem_load_read
);

  wire and_1_out, and_2_out, comparator_2_eq, comparator_3_eq, comparator_4_eq, comparator_5_eq,
       comparator_6_eq, comparator_7_eq, comparator_8_eq, comparator_9_eq, multiplexer_4_out,
       multiplexer_5_out, multiplexer_6_out, or_1_out, or_2_out;
  wire [3:0] Bin2, multiplexer_1_out, Op_Select, Shift_Select;
  wire [15:0] bit_extender_1_out;

  Comparator #(.width(2), .mode("unsigned")) comparator_1 (
    .a(Machine_Code[15:14]), .b(2'b01), .eq(Memory_Select));  // open: gt, lt
  not not_1 (Load, Machine_Code[13]);
  assign bit_extender_1_out = {{11{1'b0}}, {Machine_Code[12], Machine_Code[7:4]}};  // Bit_Extender bit_extender_1
  BitSelector #(.width(16), .group(4)) bitselector_1 (.in(Machine_Code), .out(Op_Select), .sel(2'b11));
  BitSelector #(.width(16), .group(4)) bitselector_2 (.in(Machine_Code), .out(Shift_Select), .sel(2'b01));
  BitSelector #(.width(16), .group(4)) bitselector_3 (.in(Machine_Code), .out(Bin2), .sel(2'b10));
  BitSelector #(.width(16), .group(4)) bitselector_4 (.in(Machine_Code), .out(Read_Address_2), .sel(2'b00));
  Comparator #(.width(3), .mode("unsigned")) comparator_2 (
    .a(3'b011), .b(Machine_Code[15:13]), .eq(comparator_2_eq));  // open: gt, lt
  Adder #(.width(16)) adder_1 (.a(bit_extender_1_out), .b(Read_Data_2), .out(mem_load_read));  // open: cin, cout
  Comparator #(.width(4)) comparator_3 (.a(Op_Select), .b(4'b1111), .eq(comparator_3_eq));  // open: gt, lt
  Comparator #(.width(4)) comparator_4 (.a(Op_Select), .b(4'b0011), .eq(comparator_4_eq));  // open: gt, lt
  Comparator #(.width(4)) comparator_5 (.a(Shift_Select), .b(4'b0111), .eq(comparator_5_eq));  // open: gt, lt
  and and_1 (and_1_out, comparator_4_eq, Machine_Code[7]);
  and and_2 (and_2_out, comparator_4_eq, comparator_5_eq, Machine_Code[3]);
  or or_1 (or_1_out, comparator_3_eq, and_1_out, and_2_out);
  Multiplexer #(.width(4)) multiplexer_1 (
    .in0(Shift_Select), .in1(Bin2), .out(multiplexer_1_out), .sel(or_1_out));  // open: en
  Multiplexer #(.width(4)) multiplexer_2 (
    .in0(multiplexer_1_out), .in1(Bin2), .out(Read_Address_1), .sel(comparator_2_eq));  // open: en
  Comparator #(.width(7)) comparator_6 (.a(Machine_Code[15:9]), .b(7'b0010000), .eq(comparator_6_eq));  // open: gt, lt
  Comparator #(.width(7)) comparator_7 (.a(Machine_Code[15:9]), .b(7'b0010010), .eq(comparator_7_eq));  // open: gt, lt
  Comparator #(.width(7)) comparator_8 (.a(Machine_Code[15:9]), .b(7'b0010011), .eq(comparator_8_eq));  // open: gt, lt
  Comparator #(.width(7)) comparator_9 (.a(Machine_Code[15:9]), .b(7'b0010100), .eq(comparator_9_eq));  // open: gt, lt
  Multiplexer #(.width(4)) multiplexer_3 (
    .in0(Bin2), .in1(Read_Address_2), .out(Write_Address_1), .sel(or_2_out));  // open: en
  or or_2 (or_2_out, comparator_6_eq, comparator_7_eq, comparator_8_eq, comparator_9_eq);
  Multiplexer multiplexer_4 (.in0(1'b1), .in1(1'b0), .out(multiplexer_4_out), .sel(Machine_Code[3]));  // open: en
  Multiplexer #(.select(4)) multiplexer_5 (
    .in0(1'b1), .in1(1'b1), .in2(1'b1), .in3(1'b1), .in4(1'b1), .in5(1'b1), .in6(1'b0),
    .in7(multiplexer_4_out), .in8(1'b1), .in9(1'b1), .in10(1'b1), .in11(1'b1), .in12(1'b1), .in13(1'b1),
    .in14(1'b1), .in15(1'b1), .out(multiplexer_5_out), .sel(Shift_Select));  // open: en
  Multiplexer #(.select(4)) multiplexer_6 (
    .in0(1'b1), .in1(1'b1), .in2(1'b0), .in3(1'b0), .in4(1'b0), .in5(1'b1), .in6(1'b1), .in7(1'b1),
    .in8(1'b1), .in9(1'b0), .in10(1'b0), .in11(1'b0), .in12(1'b0), .in13(1'b0), .in14(1'b0), .in15(1'b0),
    .out(multiplexer_6_out), .sel(Bin2));  // open: en
  Multiplexer #(.select(4)) multiplexer_7 (
    .in0(1'b0), .in1(1'b0), .in2(multiplexer_6_out), .in3(multiplexer_5_out), .in4(1'b1), .in5(1'b1),
    .in6(1'b0), .in7(1'b0), .in8(1'b1), .in9(1'b1), .in10(1'b1), .in11(1'b1), .in12(1'b1), .in13(1'b1),
    .in14(1'b1), .in15(1'b1), .out(register_enable), .sel(Op_Select));  // open: en
  Multiplexer #(.select(4)) multiplexer_8 (
    .in0(1'b0), .in1(1'b0), .in2(1'b0), .in3(1'b1), .in4(1'b1), .in5(1'b1), .in6(1'b0), .in7(1'b0),
    .in8(1'b1), .in9(1'b1), .in10(1'b1), .in11(1'b1), .in12(1'b1), .in13(1'b1), .in14(1'b0), .in15(1'b0),
    .out(flag_enable), .sel(Op_Select));  // open: en
  Comparator #(.width(7)) comparator_10 (.a(Machine_Code[15:9]), .b(7'b0010000), .eq(Doing_C_R));  // open: gt, lt

  assign Store = Machine_Code[13];

  // Other names for the same wires on the sheet: b3 = Machine_Code[3]

  // Notes on the sheet:
  //   Are we
  //   doing C/R?
  //   Are we doing
  //   put or getchar?
  //   Are we doing
  //   an availablility check?
  //   Are we doing
  //   a context change?
  //   shift multiplexer
  //   overall multiplexer
  //   overall multiplexer
  //   Do we have a
  //   call/return op code?
endmodule

module Legacy_Register_File (
  input  clock,
  input  [15:0] write_data,
  input  reset,
  input  [3:0] write_address,
  input  [3:0] read_address_1,
  input  [3:0] read_address_2,
  input  select,
  input  enable,
  output [15:0] read_data_1,
  output [15:0] read_data_2
);

  wire and_1_out, demultiplexer_1_out1, demultiplexer_1_out2, demultiplexer_1_out3, demultiplexer_1_out4,
       demultiplexer_1_out5, demultiplexer_1_out6, demultiplexer_1_out7, demultiplexer_1_out8,
       demultiplexer_1_out9, demultiplexer_1_out10, demultiplexer_1_out11, demultiplexer_1_out12,
       demultiplexer_1_out13, demultiplexer_1_out14, demultiplexer_1_out15;
  wire [15:0] multiplexer_1_out, multiplexer_2_out, register_1_q, register_2_q, register_3_q, register_4_q,
       register_5_q, register_6_q, register_7_q, register_8_q, register_9_q, register_10_q, register_11_q,
       register_12_q, register_13_q, register_14_q, register_15_q, register_16_q;

  and and_1 (and_1_out, select, enable);
  Demultiplexer #(.select(4)) demultiplexer_1 (
    .out1(demultiplexer_1_out1), .out2(demultiplexer_1_out2), .out3(demultiplexer_1_out3),
    .out4(demultiplexer_1_out4), .out5(demultiplexer_1_out5), .out6(demultiplexer_1_out6),
    .out7(demultiplexer_1_out7), .out8(demultiplexer_1_out8), .out9(demultiplexer_1_out9),
    .out10(demultiplexer_1_out10), .out11(demultiplexer_1_out11), .out12(demultiplexer_1_out12),
    .out13(demultiplexer_1_out13), .out14(demultiplexer_1_out14), .out15(demultiplexer_1_out15),
    .in(and_1_out), .sel(write_address));  // open: out0, en
  Register #(.width(16)) register_1 (.Q(register_1_q), .clk(clock), .clr(reset));  // open: D, en
  Register #(.width(16)) register_2 (
    .D(write_data), .en(demultiplexer_1_out1), .Q(register_2_q), .clk(clock), .clr(reset));
  Register #(.width(16)) register_3 (
    .D(write_data), .en(demultiplexer_1_out2), .Q(register_3_q), .clk(clock), .clr(reset));
  Register #(.width(16)) register_4 (
    .D(write_data), .en(demultiplexer_1_out3), .Q(register_4_q), .clk(clock), .clr(reset));
  Register #(.width(16)) register_5 (
    .D(write_data), .en(demultiplexer_1_out4), .Q(register_5_q), .clk(clock), .clr(reset));
  Register #(.width(16)) register_6 (
    .D(write_data), .en(demultiplexer_1_out5), .Q(register_6_q), .clk(clock), .clr(reset));
  Register #(.width(16)) register_7 (
    .D(write_data), .en(demultiplexer_1_out6), .Q(register_7_q), .clk(clock), .clr(reset));
  Register #(.width(16)) register_8 (
    .D(write_data), .en(demultiplexer_1_out7), .Q(register_8_q), .clk(clock), .clr(reset));
  Register #(.width(16)) register_9 (
    .D(write_data), .en(demultiplexer_1_out8), .Q(register_9_q), .clk(clock), .clr(reset));
  Register #(.width(16)) register_10 (
    .D(write_data), .en(demultiplexer_1_out9), .Q(register_10_q), .clk(clock), .clr(reset));
  Register #(.width(16)) register_11 (
    .D(write_data), .en(demultiplexer_1_out10), .Q(register_11_q), .clk(clock), .clr(reset));
  Register #(.width(16)) register_12 (
    .D(write_data), .en(demultiplexer_1_out11), .Q(register_12_q), .clk(clock), .clr(reset));
  Register #(.width(16)) register_13 (
    .D(write_data), .en(demultiplexer_1_out12), .Q(register_13_q), .clk(clock), .clr(reset));
  Register #(.width(16)) register_14 (
    .D(write_data), .en(demultiplexer_1_out13), .Q(register_14_q), .clk(clock), .clr(reset));
  Register #(.width(16)) register_15 (
    .D(write_data), .en(demultiplexer_1_out14), .Q(register_15_q), .clk(clock), .clr(reset));
  Register #(.width(16)) register_16 (
    .D(write_data), .en(demultiplexer_1_out15), .Q(register_16_q), .clk(clock), .clr(reset));
  Multiplexer #(.select(4), .width(16)) multiplexer_1 (
    .in0(register_1_q), .in1(register_2_q), .in2(register_3_q), .in3(register_4_q), .in4(register_5_q),
    .in5(register_6_q), .in6(register_7_q), .in7(register_8_q), .in8(register_9_q), .in9(register_10_q),
    .in10(register_11_q), .in11(register_12_q), .in12(register_13_q), .in13(register_14_q),
    .in14(register_15_q), .in15(register_16_q), .out(multiplexer_1_out), .sel(read_address_2));  // open: en
  Multiplexer #(.select(4), .width(16)) multiplexer_2 (
    .in0(register_1_q), .in1(register_2_q), .in2(register_3_q), .in3(register_4_q), .in4(register_5_q),
    .in5(register_6_q), .in6(register_7_q), .in7(register_8_q), .in8(register_9_q), .in9(register_10_q),
    .in10(register_11_q), .in11(register_12_q), .in12(register_13_q), .in13(register_14_q),
    .in14(register_15_q), .in15(register_16_q), .out(multiplexer_2_out), .sel(read_address_1));  // open: en
  Register #(.width(16), .trigger("high")) register_17 (
    .D(multiplexer_1_out), .Q(read_data_2), .clk(1'b1));  // open: en, clr
  Register #(.width(16), .trigger("high")) register_18 (
    .D(multiplexer_2_out), .Q(read_data_1), .clk(1'b1));  // open: en, clr

  // Notes on the sheet:
  //   feeds data to write-address register
  //   enables the write-address register
  //   zero register
  //   FP
  //   SP
endmodule

module putchar_ord (
  input  [15:0] Machine_Code,
  input  [15:0] Read_1,
  input  [15:0] Read_2,
  output T0_enable,
  output T1_enable,
  output [6:0] ASCII_code
);

  wire bitselector_1_out, comparator_1_eq;

  Comparator comparator_1 (.a(Machine_Code[15:8]), .b(8'h24), .eq(comparator_1_eq));  // open: gt, lt
  BitSelector #(.width(16)) bitselector_1 (.in(Read_1), .out(bitselector_1_out), .sel(4'b0000));
  Demultiplexer demultiplexer_1 (
    .out0(T0_enable), .out1(T1_enable), .in(comparator_1_eq), .sel(bitselector_1_out));  // open: en

  assign ASCII_code = Read_2[6:0];
endmodule

module Register_File (
  input  select,
  input  enable,
  input  reset,
  input  clock,
  input  [15:0] Write_Data_1,
  input  [15:0] Write_Data_2__Read_3,
  input  [15:0] Write_Data_3__Read_1,
  input  [3:0] Write_Address_1,
  input  [3:0] Write_Address_2,
  input  Doing_C_R,
  input  [3:0] Read_Address_1,
  input  [3:0] Read_Address_2,
  output [15:0] R4_value,
  output [15:0] R6_value,
  output [15:0] R8_value,
  output [15:0] read_data_1,
  output [15:0] read_data_2,
  output [15:0] read_data_3
);

  wire and_1_out, demultiplexer_1_out1, demultiplexer_1_out2, demultiplexer_1_out3, demultiplexer_1_out4,
       demultiplexer_1_out5, demultiplexer_1_out6, demultiplexer_1_out7, demultiplexer_1_out8,
       demultiplexer_1_out9, demultiplexer_1_out10, demultiplexer_1_out11, demultiplexer_1_out12,
       demultiplexer_1_out13, demultiplexer_1_out14, demultiplexer_1_out15, or_1_out, or_2_out, or_3_out,
       or_4_out, or_5_out, or_6_out, or_7_out, or_8_out, or_9_out, or_10_out, or_11_out, or_12_out,
       or_13_out, or_14_out, or_15_out;
  wire [1:0] demultiplexer_2_out1, demultiplexer_2_out2, demultiplexer_2_out3, demultiplexer_2_out4,
       demultiplexer_2_out5, demultiplexer_2_out6, demultiplexer_2_out7, demultiplexer_2_out8,
       demultiplexer_2_out9, demultiplexer_2_out10, demultiplexer_2_out11, demultiplexer_2_out12,
       demultiplexer_2_out13, demultiplexer_2_out14, demultiplexer_2_out15;
  wire [3:0] Write_Address_2_t, Write_Address_3;
  wire [15:0] multiplexer_1_out, multiplexer_2_out, multiplexer_3_out, multiplexer_4_out, multiplexer_5_out,
       multiplexer_6_out, multiplexer_7_out, multiplexer_8_out, multiplexer_9_out, multiplexer_10_out,
       multiplexer_11_out, multiplexer_12_out, multiplexer_13_out, multiplexer_14_out, multiplexer_15_out,
       multiplexer_18_out, multiplexer_19_out, register_1_q, register_2_q, register_3_q, register_4_q,
       register_6_q, register_8_q, register_10_q, register_11_q, register_12_q, register_13_q, register_14_q,
       register_15_q, register_16_q;

  Multiplexer #(.select(2), .width(16)) multiplexer_1 (
    .in0(Write_Data_1), .in1(Write_Data_2__Read_3), .in2(Write_Data_3__Read_1), .out(multiplexer_1_out),
    .sel(demultiplexer_2_out1));  // open: in3, en
  Multiplexer #(.select(2), .width(16)) multiplexer_2 (
    .in0(Write_Data_1), .in1(Write_Data_2__Read_3), .in2(Write_Data_3__Read_1), .out(multiplexer_2_out),
    .sel(demultiplexer_2_out2));  // open: in3, en
  Multiplexer #(.select(2), .width(16)) multiplexer_3 (
    .in0(Write_Data_1), .in1(Write_Data_2__Read_3), .in2(Write_Data_3__Read_1), .in3(Write_Data_3__Read_1),
    .out(multiplexer_3_out), .sel(demultiplexer_2_out3));  // open: en
  Multiplexer #(.select(2), .width(16)) multiplexer_4 (
    .in0(Write_Data_1), .in1(Write_Data_2__Read_3), .in2(Write_Data_3__Read_1), .in3(Write_Data_3__Read_1),
    .out(multiplexer_4_out), .sel(demultiplexer_2_out4));  // open: en
  Multiplexer #(.select(2), .width(16)) multiplexer_5 (
    .in0(Write_Data_1), .in1(Write_Data_2__Read_3), .in2(Write_Data_3__Read_1), .out(multiplexer_5_out),
    .sel(demultiplexer_2_out5));  // open: in3, en
  Multiplexer #(.select(2), .width(16)) multiplexer_6 (
    .in0(Write_Data_1), .in1(Write_Data_2__Read_3), .in2(Write_Data_3__Read_1), .out(multiplexer_6_out),
    .sel(demultiplexer_2_out6));  // open: in3, en
  Multiplexer #(.select(2), .width(16)) multiplexer_7 (
    .in0(Write_Data_1), .in1(Write_Data_2__Read_3), .in2(Write_Data_3__Read_1), .out(multiplexer_7_out),
    .sel(demultiplexer_2_out7));  // open: in3, en
  Multiplexer #(.select(2), .width(16)) multiplexer_8 (
    .in0(Write_Data_1), .in1(Write_Data_2__Read_3), .in2(Write_Data_3__Read_1), .out(multiplexer_8_out),
    .sel(demultiplexer_2_out8));  // open: in3, en
  Multiplexer #(.select(2), .width(16)) multiplexer_9 (
    .in0(Write_Data_1), .in1(Write_Data_2__Read_3), .in2(Write_Data_3__Read_1), .out(multiplexer_9_out),
    .sel(demultiplexer_2_out9));  // open: in3, en
  Multiplexer #(.select(2), .width(16)) multiplexer_10 (
    .in0(Write_Data_1), .in1(Write_Data_2__Read_3), .in2(Write_Data_3__Read_1), .out(multiplexer_10_out),
    .sel(demultiplexer_2_out10));  // open: in3, en
  Multiplexer #(.select(2), .width(16)) multiplexer_11 (
    .in0(Write_Data_1), .in1(Write_Data_2__Read_3), .in2(Write_Data_3__Read_1), .out(multiplexer_11_out),
    .sel(demultiplexer_2_out11));  // open: in3, en
  Multiplexer #(.select(2), .width(16)) multiplexer_12 (
    .in0(Write_Data_1), .in1(Write_Data_2__Read_3), .in2(Write_Data_3__Read_1), .out(multiplexer_12_out),
    .sel(demultiplexer_2_out12));  // open: in3, en
  Multiplexer #(.select(2), .width(16)) multiplexer_13 (
    .in0(Write_Data_1), .in1(Write_Data_2__Read_3), .in2(Write_Data_3__Read_1), .out(multiplexer_13_out),
    .sel(demultiplexer_2_out13));  // open: in3, en
  Multiplexer #(.select(2), .width(16)) multiplexer_14 (
    .in0(Write_Data_1), .in1(Write_Data_2__Read_3), .in2(Write_Data_3__Read_1), .out(multiplexer_14_out),
    .sel(demultiplexer_2_out14));  // open: in3, en
  Multiplexer #(.select(2), .width(16)) multiplexer_15 (
    .in0(Write_Data_1), .in1(Write_Data_2__Read_3), .in2(Write_Data_3__Read_1), .out(multiplexer_15_out),
    .sel(demultiplexer_2_out15));  // open: in3, en
  and and_1 (and_1_out, select, enable);
  Multiplexer #(.width(4)) multiplexer_16 (
    .in0(4'b0000), .in1(Write_Address_2), .out(Write_Address_2_t), .sel(Doing_C_R));  // open: en
  Multiplexer #(.width(4)) multiplexer_17 (
    .in0(4'b0000), .in1(4'b1110), .out(Write_Address_3), .sel(Doing_C_R));  // open: en
  Demultiplexer #(.select(4)) demultiplexer_1 (
    .out1(demultiplexer_1_out1), .out2(demultiplexer_1_out2), .out3(demultiplexer_1_out3),
    .out4(demultiplexer_1_out4), .out5(demultiplexer_1_out5), .out6(demultiplexer_1_out6),
    .out7(demultiplexer_1_out7), .out8(demultiplexer_1_out8), .out9(demultiplexer_1_out9),
    .out10(demultiplexer_1_out10), .out11(demultiplexer_1_out11), .out12(demultiplexer_1_out12),
    .out13(demultiplexer_1_out13), .out14(demultiplexer_1_out14), .out15(demultiplexer_1_out15),
    .in(and_1_out), .sel(Write_Address_1));  // open: out0, en
  or or_1 (or_1_out, demultiplexer_1_out1, demultiplexer_2_out1[0], demultiplexer_2_out1[1]);
  or or_2 (or_2_out, demultiplexer_1_out2, demultiplexer_2_out2[0], demultiplexer_2_out2[1]);
  or or_3 (or_3_out, demultiplexer_1_out4, demultiplexer_2_out4[0], demultiplexer_2_out4[1]);
  or or_4 (or_4_out, demultiplexer_1_out3, demultiplexer_2_out3[0], demultiplexer_2_out3[1]);
  or or_5 (or_5_out, demultiplexer_1_out5, demultiplexer_2_out5[0], demultiplexer_2_out5[1]);
  Demultiplexer #(.select(4)) demultiplexer_2 (
    .out1(demultiplexer_2_out1[0]), .out2(demultiplexer_2_out2[0]), .out3(demultiplexer_2_out3[0]),
    .out4(demultiplexer_2_out4[0]), .out5(demultiplexer_2_out5[0]), .out6(demultiplexer_2_out6[0]),
    .out7(demultiplexer_2_out7[0]), .out8(demultiplexer_2_out8[0]), .out9(demultiplexer_2_out9[0]),
    .out10(demultiplexer_2_out10[0]), .out11(demultiplexer_2_out11[0]), .out12(demultiplexer_2_out12[0]),
    .out13(demultiplexer_2_out13[0]), .out14(demultiplexer_2_out14[0]), .out15(demultiplexer_2_out15[0]),
    .in(and_1_out), .sel(Write_Address_2_t));  // open: out0, en
  or or_6 (or_6_out, demultiplexer_1_out7, demultiplexer_2_out7[0], demultiplexer_2_out7[1]);
  or or_7 (or_7_out, demultiplexer_1_out6, demultiplexer_2_out6[0], demultiplexer_2_out6[1]);
  or or_8 (or_8_out, demultiplexer_1_out9, demultiplexer_2_out9[0], demultiplexer_2_out9[1]);
  or or_9 (or_9_out, demultiplexer_1_out10, demultiplexer_2_out10[0], demultiplexer_2_out10[1]);
  or or_10 (or_10_out, demultiplexer_1_out8, demultiplexer_2_out8[0], demultiplexer_2_out8[1]);
  or or_11 (or_11_out, demultiplexer_1_out11, demultiplexer_2_out11[0], demultiplexer_2_out11[1]);
  or or_12 (or_12_out, demultiplexer_1_out12, demultiplexer_2_out12[0], demultiplexer_2_out12[1]);
  or or_13 (or_13_out, demultiplexer_1_out13, demultiplexer_2_out13[0], demultiplexer_2_out13[1]);
  or or_14 (or_14_out, demultiplexer_1_out15, demultiplexer_2_out15[0], demultiplexer_2_out15[1]);
  or or_15 (or_15_out, demultiplexer_1_out14, demultiplexer_2_out14[0], demultiplexer_2_out14[1]);
  Demultiplexer #(.select(4)) demultiplexer_3 (
    .out1(demultiplexer_2_out1[1]), .out2(demultiplexer_2_out2[1]), .out3(demultiplexer_2_out3[1]),
    .out4(demultiplexer_2_out4[1]), .out5(demultiplexer_2_out5[1]), .out6(demultiplexer_2_out6[1]),
    .out7(demultiplexer_2_out7[1]), .out8(demultiplexer_2_out8[1]), .out9(demultiplexer_2_out9[1]),
    .out10(demultiplexer_2_out10[1]), .out11(demultiplexer_2_out11[1]), .out12(demultiplexer_2_out12[1]),
    .out13(demultiplexer_2_out13[1]), .out14(demultiplexer_2_out14[1]), .out15(demultiplexer_2_out15[1]),
    .in(and_1_out), .sel(Write_Address_3));  // open: out0, en
  Register #(.width(16)) register_1 (.Q(register_1_q), .clk(clock), .clr(reset));  // open: D, en
  Register #(.width(16)) register_2 (.D(multiplexer_1_out), .en(or_1_out), .Q(register_2_q), .clk(clock), .clr(reset));
  Register #(.width(16)) register_3 (.D(multiplexer_2_out), .en(or_2_out), .Q(register_3_q), .clk(clock), .clr(reset));
  Register #(.width(16)) register_4 (.D(multiplexer_3_out), .en(or_4_out), .Q(register_4_q), .clk(clock), .clr(reset));
  Register #(.width(16)) register_5 (.D(multiplexer_4_out), .en(or_3_out), .Q(R4_value), .clk(clock), .clr(reset));
  Register #(.width(16)) register_6 (.D(multiplexer_5_out), .en(or_5_out), .Q(register_6_q), .clk(clock), .clr(reset));
  Register #(.width(16)) register_7 (.D(multiplexer_6_out), .en(or_7_out), .Q(R6_value), .clk(clock), .clr(reset));
  Register #(.width(16)) register_8 (.D(multiplexer_7_out), .en(or_6_out), .Q(register_8_q), .clk(clock), .clr(reset));
  Register #(.width(16)) register_9 (.D(multiplexer_8_out), .en(or_10_out), .Q(R8_value), .clk(clock), .clr(reset));
  Register #(.width(16)) register_10 (
    .D(multiplexer_9_out), .en(or_8_out), .Q(register_10_q), .clk(clock), .clr(reset));
  Register #(.width(16)) register_11 (
    .D(multiplexer_10_out), .en(or_9_out), .Q(register_11_q), .clk(clock), .clr(reset));
  Register #(.width(16)) register_12 (
    .D(multiplexer_11_out), .en(or_11_out), .Q(register_12_q), .clk(clock), .clr(reset));
  Register #(.width(16)) register_13 (
    .D(multiplexer_12_out), .en(or_12_out), .Q(register_13_q), .clk(clock), .clr(reset));
  Register #(.width(16)) register_14 (
    .D(multiplexer_13_out), .en(or_13_out), .Q(register_14_q), .clk(clock), .clr(reset));
  Register #(.width(16)) register_15 (
    .D(multiplexer_14_out), .en(or_15_out), .Q(register_15_q), .clk(clock), .clr(reset));
  Register #(.width(16)) register_16 (
    .D(multiplexer_15_out), .en(or_14_out), .Q(register_16_q), .clk(clock), .clr(reset));
  Multiplexer #(.select(4), .width(16)) multiplexer_18 (
    .in0(register_1_q), .in1(register_2_q), .in2(register_3_q), .in3(register_4_q), .in4(R4_value),
    .in5(register_6_q), .in6(R6_value), .in7(register_8_q), .in8(R8_value), .in9(register_10_q),
    .in10(register_11_q), .in11(register_12_q), .in12(register_13_q), .in13(register_14_q),
    .in14(register_15_q), .in15(register_16_q), .out(multiplexer_18_out), .sel(Read_Address_2));  // open: en
  Multiplexer #(.select(4), .width(16)) multiplexer_19 (
    .in0(register_1_q), .in1(register_2_q), .in2(register_3_q), .in3(register_4_q), .in4(R4_value),
    .in5(register_6_q), .in6(R6_value), .in7(register_8_q), .in8(R8_value), .in9(register_10_q),
    .in10(register_11_q), .in11(register_12_q), .in12(register_13_q), .in13(register_14_q),
    .in14(register_15_q), .in15(register_16_q), .out(multiplexer_19_out), .sel(Read_Address_1));  // open: en
  Register #(.width(16), .trigger("high")) register_17 (
    .D(multiplexer_19_out), .Q(read_data_1), .clk(1'b1));  // open: en, clr
  Register #(.width(16), .trigger("high")) register_18 (
    .D(multiplexer_18_out), .Q(read_data_2), .clk(1'b1));  // open: en, clr
  Register #(.width(16), .trigger("high")) register_19 (
    .D(register_15_q), .Q(read_data_3), .clk(1'b1));  // open: en, clr

  // Other names for the same wires on the sheet: Write_Data_2[15:0] = Write_Data_2__Read_3;
  //   Write_Data_3[15:0] = Write_Data_3__Read_1

  // Notes on the sheet:
  //   enables the Write Address registers
  //   zero register
  //   FP
  //   SP
  //   always FP
endmodule

module getchar (
  input  [15:0] Machine_Code,
  input  [15:0] Read_1,
  output Key1En,
  output Key2En,
  output Mux_Select
);

  wire comparator_1_eq;

  Comparator comparator_1 (.a(Machine_Code[15:8]), .b(8'h25), .eq(comparator_1_eq));  // open: gt, lt
  BitSelector #(.width(16)) bitselector_1 (.in(Read_1), .out(Mux_Select), .sel(4'b0000));
  Demultiplexer demultiplexer_1 (.out0(Key1En), .out1(Key2En), .in(comparator_1_eq), .sel(Mux_Select));  // open: en
endmodule

module Interrupt_Handler (
  input  [15:0] Machine_Code,
  input  key1_av,
  input  [15:0] in_infinite_loop,
  input  key2_av,
  input  [15:0] R4_value,
  input  [15:0] R6_value,
  input  [15:0] R8_value,
  output [15:0] Machine_Code_2
);

  wire and_1_out, and_2_out, and_3_out, and_4_out, comparator_1_gt, comparator_2_lt, comparator_3_eq,
       comparator_4_eq, comparator_5_eq, comparator_6_eq, or_1_out;
  wire [15:0] multiplexer_1_out, multiplexer_2_out;

  Comparator #(.width(16)) comparator_1 (.a(in_infinite_loop), .b(16'h3), .gt(comparator_1_gt));  // open: eq, lt
  Comparator #(.width(16)) comparator_2 (.a(in_infinite_loop), .b(16'hd), .lt(comparator_2_lt));  // open: gt, eq
  or or_1 (or_1_out, comparator_1_gt, comparator_2_lt);
  Comparator #(.width(16)) comparator_3 (.a(R6_value), .b(16'h1000), .eq(comparator_3_eq));  // open: gt, lt
  and and_1 (and_1_out, comparator_3_eq, comparator_4_eq);
  Comparator #(.width(16)) comparator_4 (.a(R8_value), .b(16'h2000), .eq(comparator_4_eq));  // open: gt, lt
  and and_2 (and_2_out, key1_av, and_1_out, or_1_out);
  and and_3 (and_3_out, or_1_out, and_1_out, key2_av);
  Multiplexer #(.width(16)) multiplexer_1 (
    .in0(Machine_Code), .in1(16'h2056), .out(multiplexer_1_out), .sel(and_2_out));  // open: en
  Multiplexer #(.width(16)) multiplexer_2 (
    .in0(multiplexer_1_out), .in1(16'h2078), .out(multiplexer_2_out), .sel(and_3_out));  // open: en
  Comparator #(.width(16)) comparator_5 (.a(Machine_Code), .b(16'h2200), .eq(comparator_5_eq));  // open: gt, lt
  Comparator #(.width(16)) comparator_6 (.a(16'h3000), .b(R4_value), .eq(comparator_6_eq));  // open: gt, lt
  Multiplexer #(.width(16)) multiplexer_3 (
    .in0(multiplexer_2_out), .in1(16'h2034), .out(Machine_Code_2), .sel(and_4_out));  // open: en
  and and_4 (and_4_out, comparator_5_eq, comparator_6_eq);

  // Other names for the same wires on the sheet: Mcode[15:0] = Machine_Code

  // Notes on the sheet:
  //   Registers 3, 4, 5, 6, 7, and 8 are all used for interrupt handling
endmodule
